# Fritzing sketch Pi_DMX_Board (saved by Fritzing 0.9.3b)
circuit board: 8.46667cm x 5.64444cm
breadboards: 1

parts:
  U1 = MAX485 [package=dil08]
  Raspberry_Pi_1 = Raspberry Pi 3 [part_number=RPI-3-V1.2]
  R2 = Resistor [tolerance=±5% resistance=1.6k package=THT]
  R1 = Resistor [tolerance=±5% resistance=3.3k package=THT]
  U2 = MAX485 [package=dil08]
  reset = SWITCH-MOMENTARY-2 [package=tactile-pth]
  SS = SPST Switch [package=ayz0202]
  XTAL1 = CRYSTAL - kHz [frequency="16 MHz"]
  C1 = Ceramic Capacitor [capacitance=22pF package="100 mil [THT, multilayer]"]
  C2 = Ceramic Capacitor [capacitance=22pF package="100 mil [THT, multilayer]"]
  C3 = Ceramic Capacitor [capacitance=100nF package="100 mil [THT, multilayer]"]
  R3 = Resistor [tolerance=±5% resistance=10k package=THT]
  Atmega162 = ATmega162 [package=pdpi]

nets (from the schematic view):
  N1: U1.RO, Atmega162.PD0
  GND: U1.RE, U1.DE, U1.GND, Raspberry_Pi_1.GND, R1.Pin_0, reset.1, SS.O, C1.1, C2.1, C3.0, Atmega162.GND
  VCC: U1.VCC, Raspberry_Pi_1.5V, U2.RE, U2.DE, U2.VCC
  3V3: Raspberry_Pi_1.3V3, C3.1, R3.Pin_1, Atmega162.VCC
  N2: Raspberry_Pi_1.GIPO12, reset.2, R3.Pin_0, Atmega162.RESET
  N3: Raspberry_Pi_1.GIPO24, Atmega162.PB7
  N4: Raspberry_Pi_1.GIPO23, Atmega162.PB5
  N5: Raspberry_Pi_1.GIPO18, Atmega162.PB6
  N6: Raspberry_Pi_1.GIPO15, R2.Pin_0, R1.Pin_1
  N7: Raspberry_Pi_1.GIPO14, Atmega162.PB2
  N8: R2.Pin_1, Atmega162.PB3
  N9: U2.DI, Atmega162.PD1
  N10: SS.P, Atmega162.PB4
  N11: XTAL1.pin_0, C1.0, Atmega162.XTAL1
  N12: XTAL1.pin_1, C2.0, Atmega162.XTAL2

custom parts:
  ATmega162: AVR 8-bit microcontroller.

// code stored in the sketch: Scetch for board.ino

