# Fritzing sketch Pi_DMX_Board (saved by Fritzing 0.9.3b)
circuit board: 8.46667cm x 5.64444cm
breadboards: 1

parts:
  U1 = MAX485 [package=dil08]
  Atmega162 = ATmega162 [package=pdpi]
  Raspberry_Pi_1 = Raspberry Pi 3 [part_number=RPI-3-V1.2]
  R2 = Resistor [tolerance=±5% resistance=1.6k package=THT]
  R1 = Resistor [tolerance=±5% resistance=3.3k package=THT]
  DMX_IN = XLR3_NCFAH2 [package=xlr3_nc3fah2]
  U2 = MAX485 [package=dil08]
  DMX_OUT = XLR3_NCFAH2 [package=xlr3_nc3fah2]
  reset = SWITCH-MOMENTARY-2 [package=tactile-pth]
  SS = SPST Switch [package=ayz0202]
  XTAL1 = CRYSTAL - kHz [frequency="16 MHz"]
  C1 = Ceramic Capacitor [capacitance=22pF package="100 mil [THT, multilayer]"]
  C2 = Ceramic Capacitor [capacitance=22pF package="100 mil [THT, multilayer]"]
  C3 = Ceramic Capacitor [capacitance=100nF package="100 mil [THT, multilayer]"]
  R3 = Resistor [tolerance=±5% resistance=10k package=THT]

nets:
  N1: U1.RO, Atmega162.PD0
  GND: U1.RE, U1.DE, U1.GND, Atmega162.GND, Raspberry_Pi_1.GND, R1.Pin_0, DMX_IN.1, DMX_IN.G, U2.GND, DMX_OUT.1, DMX_OUT.G, reset.1, SS.O, C1.1, C2.1, C3.0
  N2: U1.A, DMX_IN.3
  N3: U1.B, DMX_IN.2
  VCC: U1.VCC, Raspberry_Pi_1.5V, U2.RE, U2.DE, U2.VCC
  N4: Atmega162.PB2, Raspberry_Pi_1.GIPO14
  N5: Atmega162.PB3, R2.Pin_1
  N6: Atmega162.PB4, SS.P
  N7: Atmega162.PB5, Raspberry_Pi_1.GIPO23
  N8: Atmega162.PB6, Raspberry_Pi_1.GIPO18
  N9: Atmega162.PB7, Raspberry_Pi_1.GIPO24
  N10: Atmega162.RESET, Raspberry_Pi_1.GIPO12, reset.2, R3.Pin_0
  N11: Atmega162.PD1, U2.DI
  N12: Atmega162.XTAL2, XTAL1.pin_1, C2.0
  N13: Atmega162.XTAL1, XTAL1.pin_0, C1.0
  3V3: Atmega162.VCC, Raspberry_Pi_1.3v3, Raspberry_Pi_1.3V3, C3.1, R3.Pin_1
  N14: Raspberry_Pi_1.GIPO15, R2.Pin_0, R1.Pin_1
  N15: U2.A, DMX_OUT.3
  N16: U2.B, DMX_OUT.2

custom parts:
  ATmega162: AVR 8-bit microcontroller.

// code stored in the sketch: Scetch for board.ino

